// Logisim project cpu.circ as structural Verilog: 1 circuit, main circuit main
module main (
  input  CLK_RUN,
  input  [7:0] in_2,
  input  [15:0] in_3,
  input  in_4,
  input  in_5,
  input  IP_HI_TO_DATA,
  input  IP_LO_TO_DATA,
  input  DATA_TO_IR,
  input  DATA_TO_IP_HI,
  input  DATA_TO_IP_LO,
  input  IP_TO_ADDR,
  input  IP_INC,
  input  A_TO_DATA,
  input  ADDR_TO_IP,
  input  DATA_TO_A,
  input  A_TO_X,
  input  DATA_TO_MAR_HI,
  input  DATA_TO_MAR_LO,
  input  MAR_INC,
  input  ADDR_TO_MAR,
  input  Z_TO_DATA,
  input  SUB,
  input  MDR_TO_DATA,
  input  DATA_TO_MDR,
  input  H_TO_DATA,
  input  L_TO_DATA,
  input  FLAGS,
  input  DATA_TO_H,
  input  DATA_TO_L,
  input  HL_TO_ADDR,
  input  ADDR_TO_HL,
  input  DATA_TO_Y,
  input  TH_TO_DATA,
  input  TL_TO_DATA,
  input  B_TO_DATA,
  input  DATA_TO_B,
  input  DATA_TO_TH,
  input  DATA_TO_TL,
  input  T_TO_ADDR,
  input  C_TO_DATA,
  input  DATA_TO_C,
  input  SP_HI_TO_DATA,
  input  SP_LO_TO_DATA,
  input  D_TO_DATA,
  input  DATA_TO_D,
  input  DATA_TO_SP_HI,
  input  DATA_TO_SP_LO,
  input  SP_TO_ADDR,
  input  SP_DEC,
  input  SP_INC,
  input  ADDR_TO_SP,
  output [3:0] Microsequencer,
  output [7:0] out_53,
  output [15:0] out_54,
  output [15:0] out_55,
  output [7:0] out_56,
  output [7:0] out_57,
  output [15:0] out_58,
  output [7:0] out_59,
  output [7:0] out_60,
  output [7:0] out_61,
  output [7:0] out_62,
  output [7:0] out_63,
  output [15:0] out_64,
  output [7:0] _C_Z,
  output [7:0] out_66,
  output [7:0] out_67,
  output [7:0] out_68,
  output [15:0] out_69,
  output [7:0] out_70,
  output [7:0] out_71,
  output [15:0] out_72,
  output [7:0] out_73
);

  wire A_TO_DATA_t, A_TO_X_t, adder_1_cout, ADDR_TO_HL_t, ADDR_TO_IP_t, ADDR_TO_MAR_t, ADDR_TO_SP_t,
       and_1_out, and_2_out, B_TO_DATA_t, C_TO_DATA_t, CLK, CLK_STEP_out, clock_1_out, D_TO_DATA_t,
       DATA_TO_A_t, DATA_TO_B_t, DATA_TO_C_t, DATA_TO_D_t, DATA_TO_H_t, DATA_TO_IP_HI_t, DATA_TO_IP_LO_t,
       DATA_TO_IR_t, DATA_TO_L_t, DATA_TO_MAR_HI_t, DATA_TO_MAR_LO_t, DATA_TO_MDR_t, DATA_TO_SP_HI_t,
       DATA_TO_SP_LO_t, DATA_TO_TH_t, DATA_TO_TL_t, DATA_TO_Y_t, FLAGS_t, H_TO_DATA_t, HL_TO_ADDR_t, HLT,
       IP_HI_TO_DATA_t, IP_INC_t, IP_LO_TO_DATA_t, IP_TO_ADDR_t, L_TO_DATA_t, MAR_INC_t, MDR_TO_DATA_t,
       minus_CLK, nor_1_out, nor_2_out, nor_3_out, nor_4_out, nor_5_out, nor_6_out, nor_7_out, nor_8_out,
       nor_9_out, not_1_out, not_2_out, not_4_out, not_5_out, not_6_out, NXT, or_1_out, or_2_out, or_3_out,
       or_4_out, or_5_out, or_6_out, or_7_out, or_8_out, or_9_out, RST, SP_DEC_t, SP_HI_TO_DATA_t, SP_INC_t,
       SP_LO_TO_DATA_t, SP_TO_ADDR_t, SUB_t, T_TO_ADDR_t, TH_TO_DATA_t, TL_TO_DATA_t, Z_TO_DATA_t;
  wire [7:0] bit_extender_1_out, controlled_buffer_8_out, controlled_buffer_9_out, controlled_buffer_13_out,
       controlled_buffer_17_out, controlled_buffer_20_out, controlled_buffer_22_out,
       controlled_buffer_25_out, controlled_buffer_31_out, xor_1_out;
  wire [7:1] rom_1_data;
  wire [15:0] controlled_buffer_15_out;

  Button CLK_STEP (.out(CLK_STEP_out));
  Button u_RST (.out(RST));
  Clock clock_1 (.out(clock_1_out));
  and and_1 (and_1_out, clock_1_out, CLK_RUN);
  not not_1 (not_1_out, CLK_RUN);
  and and_2 (and_2_out, not_1_out, CLK_STEP_out);
  or or_1 (or_1_out, and_1_out, and_2_out);
  and and_3 (CLK, or_1_out, not_2_out);
  not not_2 (not_2_out, HLT);
  Counter #(.width(4), .max('hf)) counter_1 (
    .count(1'b1), .Q(Microsequencer), .clk(minus_CLK), .clr(or_2_out));  // open: load, D, carry
  or or_2 (or_2_out, RST, NXT);
  not not_3 (minus_CLK, CLK);
  nor nor_1 (nor_1_out, out_60[0], out_60[1], out_60[2], out_60[3], out_60[4], out_60[5], out_60[6], out_60[7]);
  D_Flip_Flop d_ff_1 (.clk(CLK), .D(nor_1_out), .Q(_C_Z[0]), .en(FLAGS), .reset(RST));  // open: Qn, preset
  D_Flip_Flop d_ff_2 (.clk(CLK), .D(adder_1_cout), .Q(_C_Z[1]), .en(FLAGS), .reset(RST));  // open: Qn, preset
  ROM #(.addrWidth(15)) rom_1 (
    .addr({Microsequencer, out_56, 1'b0, _C_Z[1:0]}), .data({rom_1_data, SP_DEC_t}), .sel(1'b1));
  Register register_1 (.D(out_53), .en(DATA_TO_IR), .Q(out_56), .clk(CLK), .clr(RST));
  Register register_2 (.D(out_53), .en(DATA_TO_A), .Q(out_57), .clk(CLK));  // open: clr
  Register register_3 (.D(out_57), .en(A_TO_X), .Q(out_59), .clk(CLK));  // open: clr
  assign bit_extender_1_out = {{7{SUB}}, SUB};  // Bit_Extender bit_extender_1
  assign xor_1_out = bit_extender_1_out ^ out_66;  // XOR_Gate xor_1, 8 bits wide
  Register register_4 (.D(out_53), .en(DATA_TO_Y), .Q(out_66), .clk(CLK));  // open: clr
  Register register_5 (.D(out_53), .en(DATA_TO_B), .Q(out_70), .clk(CLK));  // open: clr
  Register register_6 (.D(out_53), .en(DATA_TO_C), .Q(out_71), .clk(CLK));  // open: clr
  Register register_7 (.D(out_53), .en(DATA_TO_D), .Q(out_73), .clk(CLK));  // open: clr
  assign out_53 = A_TO_DATA ? out_57 : 8'bz;  // Controlled_Buffer controlled_buffer_1
  Adder adder_1 (.a(out_59), .b(xor_1_out), .out(out_60), .cin(SUB), .cout(adder_1_cout));
  assign out_53 = B_TO_DATA ? out_70 : 8'bz;  // Controlled_Buffer controlled_buffer_2
  assign out_53 = C_TO_DATA ? out_71 : 8'bz;  // Controlled_Buffer controlled_buffer_3
  assign out_53 = D_TO_DATA ? out_73 : 8'bz;  // Controlled_Buffer controlled_buffer_4
  ROM #(.addrWidth(15)) rom_2 (
    .addr({Microsequencer, out_56, 1'b0, _C_Z[1:0]}),
    .data({SP_INC_t, SP_TO_ADDR_t, ADDR_TO_SP_t, SP_LO_TO_DATA_t, DATA_TO_SP_LO_t, SP_HI_TO_DATA_t, DATA_TO_SP_HI_t, T_TO_ADDR_t}),
    .sel(1'b1));
  assign out_53 = Z_TO_DATA ? out_60 : 8'bz;  // Controlled_Buffer controlled_buffer_5
  assign out_53 = in_4 ? in_2 : 8'bz;  // Controlled_Buffer controlled_buffer_6
  assign out_53 = IP_LO_TO_DATA ? out_55[7:0] : 8'bz;  // Controlled_Buffer controlled_buffer_7
  assign controlled_buffer_8_out = DATA_TO_IP_LO ? out_53 : 8'bz;  // Controlled_Buffer controlled_buffer_8
  assign controlled_buffer_9_out = DATA_TO_MAR_LO ? out_53 : 8'bz;  // Controlled_Buffer controlled_buffer_9
  assign out_61 = DATA_TO_MDR ? out_53 : 8'bz;  // Controlled_Buffer controlled_buffer_10
  assign out_53 = MDR_TO_DATA ? out_61 : 8'bz;  // Controlled_Buffer controlled_buffer_11
  assign out_53 = L_TO_DATA ? out_63 : 8'bz;  // Controlled_Buffer controlled_buffer_12
  assign controlled_buffer_13_out = DATA_TO_L ? out_53 : 8'bz;  // Controlled_Buffer controlled_buffer_13
  assign out_53 = TL_TO_DATA ? out_68 : 8'bz;  // Controlled_Buffer controlled_buffer_14
  assign controlled_buffer_15_out[7:0] = DATA_TO_TL ? out_53 : 8'bz;  // Controlled_Buffer controlled_buffer_15
  assign out_53 = SP_LO_TO_DATA ? out_72[7:0] : 8'bz;  // Controlled_Buffer controlled_buffer_16
  assign controlled_buffer_17_out = DATA_TO_SP_LO ? out_53 : 8'bz;  // Controlled_Buffer controlled_buffer_17
  ROM #(.addrWidth(15)) rom_3 (
    .addr({Microsequencer, out_56, 1'b0, _C_Z[1:0]}),
    .data({TL_TO_DATA_t, DATA_TO_TL_t, TH_TO_DATA_t, DATA_TO_TH_t, HL_TO_ADDR_t, ADDR_TO_HL_t, L_TO_DATA_t, DATA_TO_L_t}),
    .sel(1'b1));
  assign out_53 = IP_HI_TO_DATA ? out_55[15:8] : 8'bz;  // Controlled_Buffer controlled_buffer_18
  nor nor_2 (nor_2_out, DATA_TO_IP_LO, ADDR_TO_IP);
  assign controlled_buffer_8_out = nor_2_out ? out_55[7:0] : 8'bz;  // Controlled_Buffer controlled_buffer_19
  assign controlled_buffer_20_out = DATA_TO_IP_HI ? out_53 : 8'bz;  // Controlled_Buffer controlled_buffer_20
  nor nor_3 (nor_3_out, DATA_TO_MAR_LO, ADDR_TO_MAR);
  assign controlled_buffer_9_out = nor_3_out ? out_58[7:0] : 8'bz;  // Controlled_Buffer controlled_buffer_21
  assign controlled_buffer_22_out = DATA_TO_MAR_HI ? out_53 : 8'bz;  // Controlled_Buffer controlled_buffer_22
  not not_4 (not_4_out, DATA_TO_MDR);
  assign out_53 = H_TO_DATA ? out_62 : 8'bz;  // Controlled_Buffer controlled_buffer_23
  nor nor_4 (nor_4_out, DATA_TO_L, ADDR_TO_HL);
  assign controlled_buffer_13_out = nor_4_out ? out_63 : 8'bz;  // Controlled_Buffer controlled_buffer_24
  assign controlled_buffer_25_out = DATA_TO_H ? out_53 : 8'bz;  // Controlled_Buffer controlled_buffer_25
  assign out_53 = TH_TO_DATA ? out_67 : 8'bz;  // Controlled_Buffer controlled_buffer_26
  not not_5 (not_5_out, DATA_TO_TL);
  not not_6 (not_6_out, DATA_TO_TH);
  assign controlled_buffer_15_out[7:0] = not_5_out ? out_68 : 8'bz;  // Controlled_Buffer controlled_buffer_27
  assign controlled_buffer_15_out[15:8] = DATA_TO_TH ? out_53 : 8'bz;  // Controlled_Buffer controlled_buffer_28
  assign out_53 = SP_HI_TO_DATA ? out_72[15:8] : 8'bz;  // Controlled_Buffer controlled_buffer_29
  nor nor_5 (nor_5_out, DATA_TO_SP_LO, ADDR_TO_SP);
  assign controlled_buffer_17_out = nor_5_out ? out_72[7:0] : 8'bz;  // Controlled_Buffer controlled_buffer_30
  assign controlled_buffer_31_out = DATA_TO_SP_HI ? out_53 : 8'bz;  // Controlled_Buffer controlled_buffer_31
  nor nor_6 (nor_6_out, DATA_TO_IP_HI, ADDR_TO_IP);
  assign controlled_buffer_20_out = nor_6_out ? out_55[15:8] : 8'bz;  // Controlled_Buffer controlled_buffer_32
  or or_3 (or_3_out, DATA_TO_IP_HI, DATA_TO_IP_LO, ADDR_TO_IP);
  nor nor_7 (nor_7_out, DATA_TO_MAR_HI, ADDR_TO_MAR);
  assign controlled_buffer_22_out = nor_7_out ? out_58[15:8] : 8'bz;  // Controlled_Buffer controlled_buffer_33
  or or_4 (or_4_out, DATA_TO_MAR_HI, DATA_TO_MAR_LO, ADDR_TO_MAR);
  nor nor_8 (nor_8_out, DATA_TO_H, ADDR_TO_HL);
  assign controlled_buffer_25_out = nor_8_out ? out_62 : 8'bz;  // Controlled_Buffer controlled_buffer_34
  or or_5 (or_5_out, DATA_TO_H, DATA_TO_L, ADDR_TO_HL);
  assign controlled_buffer_15_out[15:8] = not_6_out ? out_67 : 8'bz;  // Controlled_Buffer controlled_buffer_35
  or or_6 (or_6_out, DATA_TO_TH, DATA_TO_TL);
  nor nor_9 (nor_9_out, DATA_TO_SP_HI, ADDR_TO_SP);
  assign controlled_buffer_31_out = nor_9_out ? out_72[15:8] : 8'bz;  // Controlled_Buffer controlled_buffer_36
  or or_7 (or_7_out, DATA_TO_SP_HI, DATA_TO_SP_LO, ADDR_TO_SP);
  ROM #(.addrWidth(15)) rom_4 (
    .addr({Microsequencer, out_56, 1'b0, _C_Z[1:0]}),
    .data({H_TO_DATA_t, DATA_TO_H_t, MDR_TO_DATA_t, DATA_TO_MDR_t, MAR_INC_t, ADDR_TO_MAR_t, DATA_TO_MAR_LO_t, DATA_TO_MAR_HI_t}),
    .sel(1'b1));
  Register #(.width(16)) register_8 (
    .D(controlled_buffer_15_out), .en(or_6_out), .Q({out_67, out_68}), .clk(CLK), .clr(RST));
  or or_8 (or_8_out, or_7_out, SP_DEC);
  or or_9 (or_9_out, SP_DEC, SP_INC);
  Counter #(.width(16), .max('hffff)) counter_2 (
    .load(or_3_out), .D({controlled_buffer_20_out, controlled_buffer_8_out}), .count(IP_INC), .Q(out_55),
    .clk(CLK), .clr(RST));  // open: carry
  Counter #(.width(16), .max('hffff)) counter_3 (
    .load(or_4_out), .D({controlled_buffer_22_out, controlled_buffer_9_out}), .count(MAR_INC), .Q(out_58),
    .clk(CLK));  // open: carry, clr
  Register #(.width(16)) register_9 (
    .D({controlled_buffer_25_out, controlled_buffer_13_out}), .en(or_5_out), .Q({out_62, out_63}), .clk(CLK),
    .clr(RST));
  Counter #(.width(16), .max('hffff)) counter_4 (
    .load(or_8_out), .D({controlled_buffer_31_out, controlled_buffer_17_out}), .count(or_9_out), .Q(out_72),
    .clk(CLK), .clr(RST));  // open: carry
  ROM #(.addrWidth(15)) rom_5 (
    .addr({Microsequencer, out_56, 1'b0, _C_Z[1:0]}),
    .data({IP_INC_t, IP_TO_ADDR_t, ADDR_TO_IP_t, IP_LO_TO_DATA_t, DATA_TO_IP_LO_t, IP_HI_TO_DATA_t, DATA_TO_IP_HI_t, D_TO_DATA_t}),
    .sel(1'b1));
  RAM #(.addrWidth(16)) ram_1 (.addr(out_58), .data(out_61), .sel(1'b1), .clk(CLK), .ld(not_4_out));  // open: clr
  ROM #(.addrWidth(15)) rom_6 (
    .addr({Microsequencer, out_56, 1'b0, _C_Z[1:0]}),
    .data({DATA_TO_D_t, C_TO_DATA_t, DATA_TO_C_t, B_TO_DATA_t, DATA_TO_B_t, Z_TO_DATA_t, FLAGS_t, SUB_t}),
    .sel(1'b1));
  assign out_54 = in_5 ? in_3 : 16'bz;  // Controlled_Buffer controlled_buffer_37
  assign out_54 = IP_TO_ADDR ? out_55 : 16'bz;  // Controlled_Buffer controlled_buffer_38
  assign {controlled_buffer_20_out, controlled_buffer_8_out} = ADDR_TO_IP ? out_54 : 16'bz;  // Controlled_Buffer controlled_buffer_39
  assign {controlled_buffer_22_out, controlled_buffer_9_out} = ADDR_TO_MAR ? out_54 : 16'bz;  // Controlled_Buffer controlled_buffer_40
  assign out_54 = HL_TO_ADDR ? {out_62, out_63} : 16'bz;  // Controlled_Buffer controlled_buffer_41
  assign {controlled_buffer_25_out, controlled_buffer_13_out} = ADDR_TO_HL ? out_54 : 16'bz;  // Controlled_Buffer controlled_buffer_42
  assign out_54 = T_TO_ADDR ? {out_67, out_68} : 16'bz;  // Controlled_Buffer controlled_buffer_43
  assign out_54 = SP_TO_ADDR ? out_72 : 16'bz;  // Controlled_Buffer controlled_buffer_44
  assign {controlled_buffer_31_out, controlled_buffer_17_out} = ADDR_TO_SP ? out_54 : 16'bz;  // Controlled_Buffer controlled_buffer_45
  ROM #(.addrWidth(15)) rom_7 (
    .addr({Microsequencer, out_56, 1'b0, _C_Z[1:0]}),
    .data({DATA_TO_Y_t, A_TO_X_t, A_TO_DATA_t, DATA_TO_A_t, DATA_TO_IR_t, NXT, RST, HLT}), .sel(1'b1));

  assign _C_Z[7:2] = {6{1'b0}};
  assign out_64 = {out_62, out_63};
  assign out_69 = {out_67, out_68};

  // Other names for the same wires on the sheet: ZF = _C_Z[0]; CF = _C_Z[1]

  // Notes on the sheet:
  //   Clock
  //   Adder / Substractor
  //   Flags
  //   Control Unit
  //   Instruction Register
  //   A Register
  //   X Register
  //   Y Register
  //   B Register
  //   C Register
  //   D Register
  //   48-55
  //   40-47
  //   Z Register
  //   8-Bit Data Bus
  //   32-39
  //   24-31
  //   TH Register
  //   TL Register
  //   T Register
  //   16-23
  //   Instruction Pointer
  //   Memory Address Register
  //   H Register
  //   L Register
  //   HL Register
  //   Stack Pointer
  //   Memory Data Register
  //   8-15
  //   0-7
  //   16-Bit Address Bus
endmodule
